# Fritzing sketch TheGreenTeaMachine (saved by Fritzing 0.9.3b)
breadboards: 1

parts:
  LED1 = LED - 5mm [color="Red (633nm)" package="5 mm [THT]"]
  LED2 = LED - 5mm [color="Red (633nm)" package="5 mm [THT]"]
  LED3 = LED - 5mm [color="Red (633nm)" package="5 mm [THT]"]
  R1 = Resistor [tolerance=±5% resistance=220 package=THT]
  Bauteil1 = Arduino Uno (Rev3)
  R2 = Resistor [tolerance=±5% resistance=220 package=THT]
  R3 = Resistor [tolerance=±5% resistance=220 package=THT]
  S1 = Pushbutton [package="[THT]"]
  R4 = Resistor [tolerance=±5% resistance=220 package=THT]
  J1 = Piezo Speaker
  R5 = Resistor [tolerance=±5% resistance=220 package=THT]
  U3 = TEMPERATURE-SENSOR [package=to-92]  # not connected
  U4 = TMP36 [package=to-92-kit]  # not connected
  U5 = TEMPERATURE-SENSOR [package=to-92]  # not connected
  DS1 = DS18B20 1-Wire Temperature Sensor [part_number=DS18B20]
  R6 = Resistor [tolerance=±5% resistance=220 package=THT]

nets:
  N1: LED1.cathode, R2.Pin_0
  GND: LED1.anode, LED2.anode, LED3.anode, Bauteil1.GND, J1.pin1, DS1.GND
  N2: LED2.cathode, R1.Pin_0
  N3: LED3.cathode, R3.Pin_0
  N4: R1.Pin_1, Bauteil1.D10_PWM/SS
  N5: Bauteil1.D8, R3.Pin_1
  N6: Bauteil1.D9_PWM, R2.Pin_1
  N7: Bauteil1.D2, S1.Pin_1, S1.Pin_2, R4.Pin_0
  N8: Bauteil1.D5_PWM, R5.Pin_0
  N9: Bauteil1.D6_PWM, DS1.DQ, R6.Pin_1
  5V: Bauteil1.5V, S1.Pin_3, S1.Pin_4, R4.Pin_1, DS1.VDD, R6.Pin_0
  N10: J1.pin2, R5.Pin_1
